# Fritzing sketch MeubleTV (saved by Fritzing 0.9.4)

parts:
  MCU2 = Raspberry Pi Zero
  Power_plug2 = Power plug
  LPD8806_RGB_LED_Strip2 = LPD8806 RGB LED Strip
  LPD8806_RGB_LED_Strip3 = LPD8806 RGB LED Strip
  LPD8806_RGB_LED_Strip4 = LPD8806 RGB LED Strip
  Composant2 = Arduino Uno (Rev3) - ICSP
  LPD8806_RGB_LED_Strip1 = LPD8806 RGB LED Strip

nets:
  +5V: MCU2.pin_2, Power_plug2.VCC, LPD8806_RGB_LED_Strip2.+5V, LPD8806_RGB_LED_Strip3.+5V, LPD8806_RGB_LED_Strip4.+5V, Composant2.VIN, LPD8806_RGB_LED_Strip1.+5V
  GND: MCU2.pin_6, MCU2.pin_9, Power_plug2.GND, LPD8806_RGB_LED_Strip2.GND, LPD8806_RGB_LED_Strip3.GND, LPD8806_RGB_LED_Strip4.GND, Composant2.GND, LPD8806_RGB_LED_Strip1.GND
  N1: MCU2.pin_7, Composant2.RESET
  N2: MCU2.pin_8, Composant2.D0/RX
  N3: MCU2.pin_10, Composant2.D1/TX
  N4: MCU2.pin_19, LPD8806_RGB_LED_Strip4.CI, Composant2.ICSP_MOSI, Composant2.D11_PWM/MOSI
  N5: MCU2.pin_21, Composant2.ICSP_MISO, Composant2.D12/MISO
  N6: MCU2.pin_23, Composant2.ICSP_SCK
  N7: LPD8806_RGB_LED_Strip2.DI, Composant2.D8
  N8: LPD8806_RGB_LED_Strip2.CI, Composant2.D9_PWM
  N9: LPD8806_RGB_LED_Strip3.DI, Composant2.D6_PWM
  N10: LPD8806_RGB_LED_Strip3.CI, Composant2.D7
  N11: LPD8806_RGB_LED_Strip4.DI, Composant2.D10_PWM/SS
  N12: Composant2.D4, LPD8806_RGB_LED_Strip1.DI
  N13: Composant2.D5_PWM, LPD8806_RGB_LED_Strip1.CI

notes:
  DC 5V 30A
  LedStrip APA102

custom parts:
  LPD8806 RGB LED Strip: Digitally addressable RGB LED strip
